// Logisim project e2237774.circ as structural Verilog: 1 circuit, main circuit main
module main (
  input  A1,
  input  A0,
  input  B1,
  input  B0,
  output X,
  output Y,
  output Z
);

  wire and_1_out, and_2_out, and_4_out, and_5_out, and_7_out, not_1_out, not_2_out, not_3_out, not_4_out,
       not_5_out, or_1_out, or_2_out, or_3_out, or_4_out, or_5_out, or_6_out, or_7_out, or_8_out, or_9_out,
       or_10_out;

  not not_1 (not_1_out, B0);
  and and_1 (and_1_out, B1, not_1_out);
  or or_1 (or_1_out, not_1_out, B1);
  or or_2 (or_2_out, not_1_out, B1);
  not not_2 (not_2_out, A1);
  not not_3 (not_3_out, and_1_out);
  not not_4 (not_4_out, A0);
  and and_2 (and_2_out, not_2_out, or_1_out);
  or or_3 (or_3_out, not_2_out, not_4_out);
  or or_4 (or_4_out, and_2_out, and_1_out);
  not not_5 (not_5_out, B1);
  or or_5 (or_5_out, A1, B1);
  or or_6 (or_6_out, B1, B0);
  or or_7 (or_7_out, or_3_out, not_5_out);
  or or_8 (or_8_out, A1, A0);
  or or_9 (or_9_out, A0, or_6_out);
  and and_3 (Y, or_4_out, A0);
  and and_4 (and_4_out, or_8_out, not_3_out);
  and and_5 (and_5_out, and_4_out, or_2_out);
  or or_10 (or_10_out, or_8_out, B0);
  and and_6 (Z, and_5_out, or_7_out);
  and and_7 (and_7_out, or_5_out, or_10_out);
  and and_8 (X, and_7_out, or_9_out);
endmodule
