// Logisim project e2237777.circ as structural Verilog: 1 circuit, main circuit main
module main (
  input  A1,
  input  A0,
  input  B1,
  input  B0,
  input  O0,
  input  O1,
  input  O2,
  output L0,
  output L1,
  output L2,
  output L3,
  output S,
  output L7,
  output L6,
  output L5,
  output L4
);

  wire and_1_out, and_2_out, and_3_out, and_4_out, and_5_out, and_6_out, and_7_out, and_8_out,
       n2_to_4_decoder_x2_74155_1_p5, n2_to_4_decoder_x2_74155_1_p6, n2_to_4_decoder_x2_74155_1_p7,
       n2_to_4_decoder_x2_74155_1_p8, n3_to_8_decoder_74138_1_p5, n3_to_8_decoder_74138_1_p7,
       n3_to_8_decoder_74138_1_p8, n3_to_8_decoder_74138_1_p9, n3_to_8_decoder_74138_1_p10,
       n3_to_8_decoder_74138_1_p11, n3_to_8_decoder_74138_1_p12, n3_to_8_decoder_74138_1_p13,
       n3_to_8_decoder_74138_1_p14, n4_to_1_mux_x2_74153_1_p13, n4_to_1_mux_x2_74153_2_p13,
       n4_to_1_mux_x2_74153_2_p14, n4_to_1_mux_x2_74153_3_p9, n4_to_1_mux_x2_74153_4_p13,
       n4_to_1_mux_x2_74153_4_p14, n4_to_1_mux_x2_74153_5_p6, nand_1_out, nand_2_out, nand_3_out, nand_4_out,
       nand_5_out, nand_6_out, nand_7_out, nand_8_out, nand_9_out, nand_10_out, nand_11_out, nand_12_out,
       nand_13_out, nand_14_out, nand_15_out, nand_16_out, nor_1_out, nor_2_out, not_1_out, not_2_out,
       not_3_out, not_4_out, not_5_out, not_6_out, not_7_out, not_8_out, not_9_out, not_10_out, not_11_out,
       not_12_out, not_13_out, or_1_out, or_2_out, or_3_out, or_4_out, or_5_out, or_6_out, or_7_out,
       or_8_out, or_9_out, xnor_1_out, xnor_2_out, xor_1_out, xor_2_out, xor_3_out, xor_4_out, xor_5_out;

  not not_1 (not_1_out, A1);
  xor xor_1 (xor_1_out, A1, B1);
  nand nand_1 (nand_1_out, A1, B1);
  nand nand_2 (nand_2_out, A1, B1);
  or or_1 (or_1_out, A1, B1);
  or or_2 (or_2_out, B0, A1);
  not not_2 (not_2_out, A0);
  not not_3 (not_3_out, B0);
  and and_1 (and_1_out, not_1_out, B1);
  and and_2 (and_2_out, not_1_out, B0);
  and and_3 (and_3_out, not_2_out, B0);
  or or_3 (or_3_out, A1, B1);
  nand nand_3 (nand_3_out, nand_2_out, or_1_out);
  or or_4 (or_4_out, or_2_out, not_2_out);
  or or_5 (or_5_out, A0, not_3_out);
  or or_6 (or_6_out, or_5_out, B1);
  and and_4 (and_4_out, and_2_out, not_2_out);
  nand nand_4 (nand_4_out, and_3_out, B1);
  xnor xnor_1 (xnor_1_out, A0, B0);
  or or_7 (or_7_out, A0, B0);
  and and_5 (and_5_out, B1, A1);
  xor xor_2 (xor_2_out, A0, B0);
  and and_6 (and_6_out, A0, B0);
  nand nand_5 (nand_5_out, nand_1_out, nand_1_out);
  nand nand_6 (nand_6_out, nand_3_out, nand_3_out);
  and and_7 (and_7_out, or_4_out, or_6_out);
  or or_8 (or_8_out, and_1_out, and_4_out);
  nand nand_7 (nand_7_out, nand_4_out, nand_4_out);
  xnor xnor_2 (xnor_2_out, A1, B1);
  not not_4 (not_4_out, or_7_out);
  nor nor_1 (nor_1_out, or_3_out, or_3_out);
  not not_5 (not_5_out, and_5_out);
  nand nand_8 (nand_8_out, nand_6_out, and_7_out);
  nand nand_9 (nand_9_out, or_8_out, or_8_out);
  nand nand_10 (nand_10_out, nand_7_out, nand_7_out);
  nand nand_11 (nand_11_out, xnor_2_out, xnor_1_out);
  not not_6 (not_6_out, not_4_out);
  nand nand_12 (nand_12_out, B0, A0);
  nor nor_2 (nor_2_out, nor_1_out, nor_1_out);
  not not_7 (not_7_out, not_5_out);
  not not_8 (not_8_out, xor_2_out);
  and and_8 (and_8_out, and_6_out, xor_1_out);
  nand nand_13 (nand_13_out, nand_11_out, nand_11_out);
  nand nand_14 (nand_14_out, nand_12_out, nand_12_out);
  not not_9 (not_9_out, not_8_out);
  xor xor_3 (xor_3_out, xor_1_out, and_6_out);
  nand nand_15 (nand_15_out, nand_8_out, nand_8_out);
  nand nand_16 (nand_16_out, nand_9_out, nand_10_out);
  xor xor_4 (xor_4_out, A0, B0);
  xor xor_5 (xor_5_out, A1, B1);
  or or_9 (or_9_out, and_8_out, nand_5_out);
  // _4_to_1_MUX__x2___74153 #(.Facing("east")) 4_to_1_mux_x2_74153_1: pin names not known; wires that end beside it: 1'b0, 1'b0, nand_16_out, 1'b0, 1'b0, 1'b0, 1'b0, 1'b0, 1'b0, O0, 1'b0, O2, n4_to_1_mux_x2_74153_1_p13
  not not_10 (not_10_out, not_6_out);
  not not_11 (not_11_out, nor_2_out);
  // _4_to_1_MUX__x2___74153 #(.Facing("east")) 4_to_1_mux_x2_74153_2: pin names not known; wires that end beside it: not_9_out, not_9_out, nand_13_out, not_9_out, nand_15_out, xor_3_out, 1'b0, not_9_out, 1'b0, O0, 1'b0, O1, n4_to_1_mux_x2_74153_2_p13, n4_to_1_mux_x2_74153_2_p14
  // _4_to_1_MUX__x2___74153 #(.Facing("east")) 4_to_1_mux_x2_74153_3: pin names not known; wires that end beside it: 1'b0, or_9_out, 1'b0, 1'b0, 1'b0, O0, 1'b0, O1, n4_to_1_mux_x2_74153_3_p9
  // _4_to_1_MUX__x2___74153 #(.Facing("east")) 4_to_1_mux_x2_74153_4: pin names not known; wires that end beside it: not_6_out, nand_14_out, not_10_out, xor_4_out, nor_2_out, not_7_out, not_11_out, xor_5_out, 1'b0, O0, 1'b0, O1, n4_to_1_mux_x2_74153_4_p13, n4_to_1_mux_x2_74153_4_p14
  not not_12 (not_12_out, O2);
  // _4_to_1_MUX__x2___74153 #(.Facing("east")) 4_to_1_mux_x2_74153_5: pin names not known; wires that end beside it: 1'b0, 1'b0, n4_to_1_mux_x2_74153_1_p13, 1'b0, 1'b0, n4_to_1_mux_x2_74153_5_p6, 1'b0, 1'b0, 1'b0, O1, 1'b0, O2, S, S
  not not_13 (not_13_out, 1'b0);
  not not_14 (n4_to_1_mux_x2_74153_5_p6, not_13_out);
  // _2_to_4_Decoder__x2___74155 #(.Facing("east")) 2_to_4_decoder_x2_74155_1: pin names not known; wires that end beside it: n4_to_1_mux_x2_74153_4_p13, n4_to_1_mux_x2_74153_4_p14, O2, not_12_out, n2_to_4_decoder_x2_74155_1_p5, n2_to_4_decoder_x2_74155_1_p6, n2_to_4_decoder_x2_74155_1_p7, n2_to_4_decoder_x2_74155_1_p8
  // _3_to_8_decoder__74138 #(.Facing("east")) 3_to_8_decoder_74138_1: pin names not known; wires that end beside it: n4_to_1_mux_x2_74153_2_p13, n4_to_1_mux_x2_74153_2_p14, n4_to_1_mux_x2_74153_3_p9, O2, n3_to_8_decoder_74138_1_p5, n3_to_8_decoder_74138_1_p5, n3_to_8_decoder_74138_1_p7, n3_to_8_decoder_74138_1_p8, n3_to_8_decoder_74138_1_p9, n3_to_8_decoder_74138_1_p10, n3_to_8_decoder_74138_1_p11, n3_to_8_decoder_74138_1_p12, n3_to_8_decoder_74138_1_p13, n3_to_8_decoder_74138_1_p14
  not not_15 (n3_to_8_decoder_74138_1_p5, O2);
  nand nand_17 (L3, n2_to_4_decoder_x2_74155_1_p8, n3_to_8_decoder_74138_1_p10);
  nand nand_18 (L2, n2_to_4_decoder_x2_74155_1_p7, n3_to_8_decoder_74138_1_p9);
  nand nand_19 (L0, n2_to_4_decoder_x2_74155_1_p5, n3_to_8_decoder_74138_1_p7);
  nand nand_20 (L1, n2_to_4_decoder_x2_74155_1_p6, n3_to_8_decoder_74138_1_p8);
  nor nor_3 (L4, n3_to_8_decoder_74138_1_p11, n3_to_8_decoder_74138_1_p11);
  not not_16 (L5, n3_to_8_decoder_74138_1_p12);
  not not_17 (L6, n3_to_8_decoder_74138_1_p13);
  not not_18 (L7, n3_to_8_decoder_74138_1_p14);
endmodule
